// Logisim project CPU_simulation.circ as structural Verilog: 5 circuits, main circuit CPU_main
module CPU_main (
  input  GreaterThanButton,
  input  LessThanButton,
  output [6:0] TTY_Data,
  output Clockk,
  output WriteEnable,
  output Clear_TTY
);

  wire alu_1_acc_ne_zero, and_1_out, clock_1_out, instruction_decoding_unit_1_bnez,
       instruction_decoding_unit_1_get_input, instruction_decoding_unit_1_notstop,
       instruction_decoding_unit_1_use_memory, instruction_decoding_unit_1_write_acc,
       instruction_decoding_unit_1_write_memory, multiplexer_2_out, or_1_out;
  wire [3:0] instruction_decoding_unit_1_alu_operation;
  wire [7:0] adder_1_out, alu_1_alu_to_acc, Data_Memory_dout, instruction_decoding_unit_1_addr_or_imm,
       multiplexer_1_out, multiplexer_3_out, multiplexer_4_out, PC_q;
  wire [7:7] ACC_q;
  wire [15:0] Instruction_Memory_data;

  Adder adder_1 (.a(PC_q), .b(8'h1), .out(adder_1_out));  // open: cin, cout
  Register PC (.D(multiplexer_1_out), .en(1'b1), .clk(Clockk), .Q(PC_q));  // open: clr
  Multiplexer #(.width(8)) multiplexer_1 (
    .in0(adder_1_out), .in1(instruction_decoding_unit_1_addr_or_imm), .out(multiplexer_1_out), .sel(and_1_out));
  and and_1 (and_1_out, alu_1_acc_ne_zero, instruction_decoding_unit_1_bnez);
  Instruction_Decoding_Unit instruction_decoding_unit_1 (
    .Instruction(Instruction_Memory_data), .ALU_Operation(instruction_decoding_unit_1_alu_operation),
    .Write_ACC(instruction_decoding_unit_1_write_acc), .Use_Memory(instruction_decoding_unit_1_use_memory),
    .Write_Memory(instruction_decoding_unit_1_write_memory), .BNEZ(instruction_decoding_unit_1_bnez),
    .Output_Char(WriteEnable), .Clear_TTY(Clear_TTY), .Get_Input(instruction_decoding_unit_1_get_input),
    .NotStop(instruction_decoding_unit_1_notstop), .Addr_or_Imm(instruction_decoding_unit_1_addr_or_imm));
  Clock clock_1 (.out(clock_1_out));
  and and_2 (Clockk, clock_1_out, multiplexer_2_out);
  Multiplexer multiplexer_2 (
    .in0(instruction_decoding_unit_1_notstop), .in1(or_1_out), .out(multiplexer_2_out),
    .sel(instruction_decoding_unit_1_get_input));
  RAM #(.asyncread("true"), .clearpin("true")) Data_Memory (
    .addr(instruction_decoding_unit_1_addr_or_imm), .we(instruction_decoding_unit_1_write_memory),
    .clk(Clockk), .din({ACC_q[7], TTY_Data}), .dout(Data_Memory_dout));  // open: oe, clr
  ROM #(.dataWidth(16)) Instruction_Memory (.addr(PC_q), .data(Instruction_Memory_data));
  Multiplexer #(.width(8)) multiplexer_3 (
    .in0(instruction_decoding_unit_1_addr_or_imm), .in1(Data_Memory_dout), .out(multiplexer_3_out),
    .sel(instruction_decoding_unit_1_use_memory));
  Register ACC (
    .D(alu_1_alu_to_acc), .en(instruction_decoding_unit_1_write_acc), .clk(Clockk), .Q({ACC_q[7], TTY_Data}));  // open: clr
  ALU alu_1 (
    .ALU_Operation(instruction_decoding_unit_1_alu_operation), .From_ACC({ACC_q[7], TTY_Data}),
    .Input2(multiplexer_3_out), .Clock(Clockk), .Button_Type(multiplexer_4_out),
    .ACC_NE_Zero(alu_1_acc_ne_zero), .ALU_to_ACC(alu_1_alu_to_acc));
  or or_1 (or_1_out, LessThanButton, GreaterThanButton);
  Multiplexer #(.width(8)) multiplexer_4 (
    .in0({8{1'b0}}), .in1(8'h1), .out(multiplexer_4_out), .sel(GreaterThanButton));

  // Notes on the sheet:
  //   contents of Instruction_Memory (hex, n*v repeats v):
  //   2022 10ff 3002 5048 5069 5067 5068 5065 5072 5020 506f 5072 5020 504c 506f 5077 5065 5072 500a 502d
  //   5054 5077 506f 5020 506e 5075 506d 5062 5065 5072 5073 5020 5067 5065 506e 5065 5072 5061 5074 5065
  //   5064 500a 502d 5059 506f 5075 5020 5073 5065 5065 5020 506f 506e 5065 502c 5020 5067 5075 5065 5073
  //   5073 5020 5069 5066 5020 5068 5069 5064 5064 5065 506e 5020 5069 5073 5020 5068 5069 5067 5068 5065
  //   5072 502f 506c 506f 5077 5065 5072 500a 502d 5052 5069 5067 5068 5074 5020 503d 5020 5063 506f 506e
  //   5074 5069 506e 5075 5065 502c 5020 5057 5072 506f 506e 5067 5020 503d 5020 506c 506f 5073 5065 500a
  //   502d 5050 5072 5065 5073 5073 5020 5061 506e 5079 5020 506b 5065 5079 5000 7000 1700 3000 1700 3001
  //   2002 1101 3002 2000 2501 3003 6000 1069 5000 1073 5000 1020 5000 2000 1a64 1601 5000 2000 1a0a 1b0a
  //   1601 5000 2000 1b0a 1601 5000 5020 5048 5069 5067 5068 5065 5072 5020 506f 5072 5020 504c 506f 5077
  //   5065 5072 5020 7000 1800 2903 4088 6000 5047 5061 506d 5065 5020 504f 5076 5065 5072 5021 500a 5053
  //   5063 506f 5072 5065 503a 5020 2002 1a64 1601 5000 2002 1a0a 1b0a 1601 5000 2002 1b0a 1601 5000 500a
  //   5050 5072 5065 5073 5073 5020 5061 506e 5079 5020 506b 5065 5079 5020 5074 506f 5020 5070 506c 5061
  //   5079 5020 5061 5067 5061 5069 506e 5000 7000 1001 6000 4000 f000
  //   Student id: 25869720
endmodule

module Instruction_Decoding_Unit (
  input  [15:0] Instruction,
  output [3:0] ALU_Operation,
  output Write_ACC,
  output Use_Memory,
  output Write_Memory,
  output BNEZ,
  output Output_Char,
  output Clear_TTY,
  output Get_Input,
  output NotStop,
  output [7:0] Addr_or_Imm
);

  wire decoder_1_out1, decoder_1_out2, decoder_1_out15, or_1_out;

  Decoder #(.select(4)) decoder_1 (
    .out1(decoder_1_out1), .out2(decoder_1_out2), .out3(Write_Memory), .out4(BNEZ), .out5(Output_Char),
    .out6(Clear_TTY), .out7(Get_Input), .out15(decoder_1_out15), .sel(Instruction[15:12]));  // open: out0, out8, out9, out10, out11, out12, out13, out14, en
  or or_1 (or_1_out, decoder_1_out2, Output_Char);
  or or_2 (Write_ACC, decoder_1_out1, or_1_out);
  or or_3 (Use_Memory, decoder_1_out2, Write_Memory);
  not not_1 (NotStop, decoder_1_out15);

  assign Addr_or_Imm = Instruction[7:0];
  assign ALU_Operation = Instruction[11:8];
endmodule

module ALU (
  input  [3:0] ALU_Operation,
  input  [7:0] From_ACC,
  input  [7:0] Input2,
  input  Clock,
  input  [7:0] Button_Type,
  output ACC_NE_Zero,
  output [7:0] ALU_to_ACC
);

  wire [0:0] comparator_1_eq, comparator_1_gt;
  wire [7:0] adder_1_out, convert_to_ascii_1_ascii_equivalent, divider_1_out, divider_1_rem, nand_1_out,
       or_1_out, random_1_out, shifter_1_out;

  Adder adder_1 (.a(From_ACC), .b(Input2), .out(adder_1_out));  // open: cin, cout
  assign nand_1_out = ~(From_ACC & Input2);  // NAND_Gate nand_1, 8 bits wide
  assign or_1_out = From_ACC | Input2;  // OR_Gate or_1, 8 bits wide
  Shifter #(.shift("lr")) shifter_1 (.in(From_ACC), .\dist (3'b100), .out(shifter_1_out));
  Comparator #(.mode("unsigned")) comparator_1 (
    .a(From_ACC), .b(Input2), .gt(comparator_1_gt[0]), .eq(comparator_1_eq[0]));  // open: lt
  Random random_1 (.clr(1'b0), .next(1'b1), .clk(Clock), .out(random_1_out));
  Divider divider_1 (.a(From_ACC), .b(Input2), .out(divider_1_out), .rem(divider_1_rem));  // open: upper
  Comparator comparator_2 (.a(From_ACC), .b({8{1'b0}}), .gt(ACC_NE_Zero));  // open: eq, lt
  Convert_To_ASCII convert_to_ascii_1 (
    .rawHex(From_ACC), .WhichNibble(Input2[0]), .Ascii_Equivalent(convert_to_ascii_1_ascii_equivalent));
  Multiplexer #(.select(4), .width(8)) multiplexer_1 (
    .in0(Input2), .in1(adder_1_out), .in2(nand_1_out), .in3(or_1_out), .in4(shifter_1_out),
    .in5({{7{1'b0}}, comparator_1_gt[0]}), .in6(convert_to_ascii_1_ascii_equivalent), .in7(random_1_out),
    .in8(Button_Type), .in9({{7{1'b0}}, comparator_1_eq[0]}), .in10(divider_1_out), .in11(divider_1_rem),
    .out(ALU_to_ACC), .sel(ALU_Operation));  // open: in12, in13, in14, in15
endmodule

module Convert_To_ASCII (
  input  [7:0] rawHex,
  input  WhichNibble,
  output [7:0] Ascii_Equivalent
);

  wire comparator_1_gt;
  wire [3:0] multiplexer_1_out;
  wire [7:0] multiplexer_2_out;

  Multiplexer #(.width(4)) multiplexer_1 (
    .in0(rawHex[7:4]), .in1(rawHex[3:0]), .out(multiplexer_1_out), .sel(WhichNibble));
  Multiplexer #(.width(8)) multiplexer_2 (.in0(8'h37), .in1(8'h30), .out(multiplexer_2_out), .sel(comparator_1_gt));
  Comparator #(.mode("unsigned"), .width(4)) comparator_1 (
    .a(4'b1010), .b(multiplexer_1_out), .gt(comparator_1_gt));  // open: eq, lt
  Adder adder_1 (.a({4'b0000, multiplexer_1_out}), .b(multiplexer_2_out), .out(Ascii_Equivalent));  // open: cin, cout
endmodule

module Game_Higher_Or_Lower (
);

  wire cpu_main_1_clear_tty, cpu_main_1_clockk, cpu_main_1_writeenable, GreaterThan_out, LessThanOrEqual_out;
  wire [6:0] cpu_main_1_tty_data;

  Button GreaterThan (.out(GreaterThan_out));
  Button LessThanOrEqual (.out(LessThanOrEqual_out));
  TTY #(.cols(39)) tty_1 (
    .data(cpu_main_1_tty_data), .clk(cpu_main_1_clockk), .we(cpu_main_1_writeenable),
    .clr(cpu_main_1_clear_tty));
  CPU_main cpu_main_1 (
    .GreaterThanButton(GreaterThan_out), .LessThanButton(LessThanOrEqual_out),
    .TTY_Data(cpu_main_1_tty_data), .Clockk(cpu_main_1_clockk), .WriteEnable(cpu_main_1_writeenable),
    .Clear_TTY(cpu_main_1_clear_tty));
endmodule
